# Fritzing sketch esp32-s3-devkit-c-breadboard (saved by Fritzing 1.0.3b)
breadboards: 1

parts:
  LED1 = LED - 5mm [color="Red (633nm)" current=0.030A package="5 mm [THT]"]
  R1 = Resistor [tolerance=±5% resistance=220 package="0603 [SMD]"]

nets:
  N1: LED1.cathode, R1.Pin_0
