# Fritzing sketch xiao-esp32-s3-breadboard (saved by Fritzing 1.0.3b)
breadboards: 1

parts:
  LED1 = LED - 5mm [color="Red (633nm)" current=0.030A package="5 mm [THT]"]
  R1 = Resistor [tolerance=±5% resistance=220 package="0603 [SMD]"]
  XIAO_ESP32S1 = XIAO ESP32S3 [package="DIP (Dual Inline) [THT]"]

nets:
  N1: LED1.cathode, R1.Pin_1
  N2: LED1.anode, XIAO_ESP32S1.D3
  N3: R1.Pin_0, XIAO_ESP32S1.GND

custom parts:
  XIAO ESP32S3: Seeed Studio XIAO ESP32S3 leverages 240MHz Xtensa 32-bit LX7 dual-core processor, supporting both WiFi and BLE 5.0 wireless connectivities, a 2.4GHz Rod antenna, allows for deep sleep mode with power consumption as low as 14μA while supporting lithium battery charging management. Ideal for the Internet of Things, Smart Homes, Wireless wearable devices, Robotics, etc.
